// Logisim project control-logic.circ as structural Verilog: 1 circuit, main circuit control_logic
module control_logic (
  input  [31:0] Instruction,
  input  BrEq,
  input  BrLt,
  output PCSel,
  output RegWEn,
  output [2:0] ImmSel,
  output BrUn,
  output ASel,
  output BSel,
  output [3:0] ALUSel,
  output MemWEn,
  output [1:0] WBSel
);

  wire and_26_out, and_27_out, and_28_out, and_29_out, and_30_out, and_31_out, funct3_0x0, funct3_0x1,
       funct3_0x2, funct3_0x3, funct3_0x4, funct3_0x5, funct3_0x6, funct3_0x7, funct7_0x00, funct7_0x01,
       funct7_0x20, is_add, is_addi, is_and, is_andi, is_auipc, is_beq, is_bge, is_bgeu, is_blt, is_bltu,
       is_bne, is_jal, is_jalr, is_lb, is_lh, is_lui, is_lw, is_mul, is_mulh, is_mulhu, is_or, is_ori, is_sb,
       is_sh, is_sll, is_slli, is_slt, is_slti, is_sra, is_srai, is_srl, is_srli, is_sub, is_sw, is_xor,
       is_xori, not_1_out, not_2_out, opcode_0x03, opcode_0x13, opcode_0x23, opcode_0x33, opcode_0x63,
       opcode_0x67;
  wire [5:0] ROMInput;
  wire [15:14] rom_1_data;

  Comparator #(.width(7)) comparator_1 (.a(Instruction[6:0]), .b(7'b0110011), .eq(opcode_0x33));  // open: gt, lt
  Comparator #(.width(7)) comparator_2 (.a(Instruction[6:0]), .b(7'b0000011), .eq(opcode_0x03));  // open: gt, lt
  Comparator #(.width(7)) comparator_3 (.a(Instruction[6:0]), .b(7'b0010011), .eq(opcode_0x13));  // open: gt, lt
  Comparator #(.width(7)) comparator_4 (.a(Instruction[6:0]), .b(7'b0100011), .eq(opcode_0x23));  // open: gt, lt
  Comparator #(.width(7)) comparator_5 (.a(Instruction[6:0]), .b(7'b1100011), .eq(opcode_0x63));  // open: gt, lt
  Comparator #(.width(7)) comparator_6 (.a(Instruction[6:0]), .b(7'b0010111), .eq(is_auipc));  // open: gt, lt
  Comparator #(.width(7)) comparator_7 (.a(Instruction[6:0]), .b(7'b0110111), .eq(is_lui));  // open: gt, lt
  Comparator #(.width(7)) comparator_8 (.a(Instruction[6:0]), .b(7'b1101111), .eq(is_jal));  // open: gt, lt
  Comparator #(.width(7)) comparator_9 (.a(Instruction[6:0]), .b(7'b1100111), .eq(opcode_0x67));  // open: gt, lt
  and and_1 (is_add, opcode_0x33, funct3_0x0, funct7_0x00);
  and and_2 (is_mulh, opcode_0x33, funct3_0x1, funct7_0x01);
  and and_3 (is_srl, opcode_0x33, funct3_0x5, funct7_0x00);
  and and_4 (is_lb, opcode_0x03, funct3_0x0);
  and and_5 (is_slli, opcode_0x13, funct3_0x1, funct7_0x00);
  and and_6 (is_srai, opcode_0x13, funct3_0x5, funct7_0x20);
  and and_7 (is_sh, opcode_0x23, funct3_0x1);
  and and_8 (is_blt, opcode_0x63, funct3_0x4);
  and and_9 (is_jalr, opcode_0x67, funct3_0x0);
  ROM #(.addrWidth(6), .dataWidth(16)) rom_1 (
    .addr(ROMInput), .data({rom_1_data, WBSel, MemWEn, ALUSel, BSel, ASel, BrUn, ImmSel, RegWEn}));
  and and_10 (is_mul, opcode_0x33, funct3_0x0, funct7_0x01);
  and and_11 (is_mulhu, opcode_0x33, funct3_0x3, funct7_0x01);
  and and_12 (is_sra, opcode_0x33, funct3_0x5, funct7_0x20);
  and and_13 (is_lh, opcode_0x03, funct3_0x1);
  and and_14 (is_slti, opcode_0x13, funct3_0x2);
  and and_15 (is_ori, opcode_0x13, funct3_0x6);
  and and_16 (is_sw, opcode_0x23, funct3_0x2);
  and and_17 (is_bge, opcode_0x63, funct3_0x5);
  Comparator #(.width(3)) comparator_10 (.a(Instruction[14:12]), .b(3'b000), .eq(funct3_0x0));  // open: gt, lt
  Comparator #(.width(3)) comparator_11 (.a(Instruction[14:12]), .b(3'b001), .eq(funct3_0x1));  // open: gt, lt
  Comparator #(.width(3)) comparator_12 (.a(Instruction[14:12]), .b(3'b010), .eq(funct3_0x2));  // open: gt, lt
  Comparator #(.width(3)) comparator_13 (.a(Instruction[14:12]), .b(3'b011), .eq(funct3_0x3));  // open: gt, lt
  Comparator #(.width(3)) comparator_14 (.a(Instruction[14:12]), .b(3'b100), .eq(funct3_0x4));  // open: gt, lt
  Comparator #(.width(3)) comparator_15 (.a(Instruction[14:12]), .b(3'b101), .eq(funct3_0x5));  // open: gt, lt
  Comparator #(.width(3)) comparator_16 (.a(Instruction[14:12]), .b(3'b110), .eq(funct3_0x6));  // open: gt, lt
  Comparator #(.width(3)) comparator_17 (.a(Instruction[14:12]), .b(3'b111), .eq(funct3_0x7));  // open: gt, lt
  or or_1 (PCSel, and_26_out, and_27_out, and_28_out, and_29_out, and_30_out, and_31_out, is_jal, is_jalr);
  and and_18 (is_sub, opcode_0x33, funct3_0x0, funct7_0x20);
  and and_19 (is_slt, opcode_0x33, funct3_0x2, funct7_0x00);
  and and_20 (is_or, opcode_0x33, funct3_0x6, funct7_0x00);
  and and_21 (is_lw, opcode_0x03, funct3_0x2);
  and and_22 (is_xori, opcode_0x13, funct3_0x4);
  and and_23 (is_andi, opcode_0x13, funct3_0x7);
  and and_24 (is_beq, opcode_0x63, funct3_0x0);
  and and_25 (is_bltu, opcode_0x63, funct3_0x6);
  Priority_Encoder #(.select_enc(6)) priority_encoder_1 (
    .in0(is_add), .in1(is_mul), .in2(is_sub), .in3(is_sll), .in4(is_mulh), .in5(is_mulhu), .in6(is_slt),
    .in7(is_xor), .in8(is_srl), .in9(is_sra), .in10(is_or), .in11(is_and), .in12(is_lb), .in13(is_lh),
    .in14(is_lw), .in15(is_addi), .in16(is_slli), .in17(is_slti), .in18(is_xori), .in19(is_srli),
    .in20(is_srai), .in21(is_ori), .in22(is_andi), .in23(is_sb), .in24(is_sh), .in25(is_sw), .in26(is_beq),
    .in27(is_bne), .in28(is_blt), .in29(is_bge), .in30(is_bltu), .in31(is_bgeu), .in32(is_auipc),
    .in33(is_lui), .in34(is_jal), .in35(is_jalr), .out(ROMInput));  // open: in36, in37, in38, in39, in40, in41, in42, in43, in44, in45, in46, in47, in48, in49, in50, in51, in52, in53, in54, in55, in56, in57, in58, in59, in60, in61, in62, in63, gs, en_out, en_in
  Comparator #(.width(7)) comparator_18 (.a(Instruction[31:25]), .b({7{1'b0}}), .eq(funct7_0x00));  // open: gt, lt
  Comparator #(.width(7)) comparator_19 (.a(Instruction[31:25]), .b(7'b0000001), .eq(funct7_0x01));  // open: gt, lt
  Comparator #(.width(7)) comparator_20 (.a(Instruction[31:25]), .b(7'b0100000), .eq(funct7_0x20));  // open: gt, lt
  and and_26 (and_26_out, is_beq, BrEq);
  and and_27 (and_27_out, is_bne, not_1_out);
  and and_28 (and_28_out, is_blt, BrLt);
  and and_29 (and_29_out, is_bltu, BrLt);
  and and_30 (and_30_out, is_bge, not_2_out);
  and and_31 (and_31_out, is_bgeu, not_2_out);
  not not_1 (not_1_out, BrEq);
  and and_32 (is_sll, opcode_0x33, funct3_0x1, funct7_0x00);
  and and_33 (is_xor, opcode_0x33, funct3_0x4, funct7_0x00);
  and and_34 (is_and, opcode_0x33, funct3_0x7, funct7_0x00);
  and and_35 (is_addi, opcode_0x13, funct3_0x0);
  and and_36 (is_srli, opcode_0x13, funct3_0x5, funct7_0x00);
  and and_37 (is_sb, opcode_0x23, funct3_0x0);
  and and_38 (is_bne, opcode_0x63, funct3_0x1);
  and and_39 (is_bgeu, opcode_0x63, funct3_0x7);
  not not_2 (not_2_out, BrLt);

  // Other names for the same wires on the sheet: opcode[6:0] = Instruction[6:0]; funct3[2:0] = Instruction[14:12];
  //   funct7[6:0] = Instruction[31:25]

  // Notes on the sheet:
  //   INPUTS to your circuit
  //   Connect ROM Input here ->
  //   contents of rom_1 (hex, n*v repeats v):
  //   1001 1401 1601 1081 1481 1581 1101 1201 1281 1681 1301 1381 41 41 41 1041 10c1 1141 1241 12c1 16c1
  //   1341 13c1 842 842 842 4*64 74 74 1067 17e7 2069 2041
  //   ROM FOR CONTROL LOGIC
  //   DON'T CHANGE THE LOCATIONS OF THE INPUTS AND OUTPUTS!
  //   This is only if you choose to do the ROM option
  //   CONNECT
  //   WIRE
  //   TO
  //   USE
  //   ROM
  //   OUTPUT from your circuit
  //   Reminder: If using ROM, use combinational logic for PCSel
endmodule
